// Logisim project 10.12scpu.circ as structural Verilog: 37 circuits, main circuit Decoder2to4
module Decoder2to4 (
  input  A0,
  input  A1,
  input  EN,
  output Q0,
  output Q1,
  output Q2,
  output Q3
);

  wire not_1_out, not_2_out;

  not not_1 (not_1_out, A1);
  not not_2 (not_2_out, A0);
  and and_1 (Q0, not_1_out, EN, not_2_out);
  and and_2 (Q1, not_1_out, EN, A0);
  and and_3 (Q2, A1, EN, not_2_out);
  and and_4 (Q3, A1, EN, A0);
endmodule

module Decoder3to8 (
  input  A2,
  input  A1,
  input  A0,
  input  EN,
  output Q0,
  output Q1,
  output Q2,
  output Q3,
  output Q4,
  output Q5,
  output Q6,
  output Q7
);

  wire and_1_out, and_2_out, not_1_out;

  not not_1 (not_1_out, A2);
  and and_1 (and_1_out, not_1_out, EN);
  and and_2 (and_2_out, A2, EN);
  Decoder2to4 Decoder2to4_1 (.A0(A1), .A1(A0), .EN(and_1_out), .Q0(Q0), .Q1(Q1), .Q2(Q2), .Q3(Q3));
  Decoder2to4 Decoder2to4_2 (.A0(A1), .A1(A0), .EN(and_2_out), .Q0(Q4), .Q1(Q5), .Q2(Q6), .Q3(Q7));
endmodule

module SevenSegDecoder_1 (
  input  A0,
  input  A1,
  input  A2,
  input  A3,
  input  EN,
  output A,
  output B,
  output C,
  output D,
  output E,
  output F,
  output G,
  output point
);

  wire decoder4to16_1_q0, decoder4to16_1_q1, decoder4to16_1_q2, decoder4to16_1_q3, decoder4to16_1_q4,
       decoder4to16_1_q5, decoder4to16_1_q6, decoder4to16_1_q7, decoder4to16_1_q8, decoder4to16_1_q9,
       decoder4to16_1_q10, decoder4to16_1_q11, decoder4to16_1_q12, decoder4to16_1_q13, decoder4to16_1_q14,
       decoder4to16_1_q15;

  Decoder4to16 decoder4to16_1 (
    .A3(A3), .A2(A2), .A1(A1), .A0(A0), .EN(EN), .Q0(decoder4to16_1_q0), .Q1(decoder4to16_1_q1),
    .Q2(decoder4to16_1_q2), .Q3(decoder4to16_1_q3), .Q4(decoder4to16_1_q4), .Q5(decoder4to16_1_q5),
    .Q6(decoder4to16_1_q6), .Q7(decoder4to16_1_q7), .Q8(decoder4to16_1_q8), .Q9(decoder4to16_1_q9),
    .Q10(decoder4to16_1_q10), .Q11(decoder4to16_1_q11), .Q12(decoder4to16_1_q12), .Q13(decoder4to16_1_q13),
    .Q14(decoder4to16_1_q14), .Q15(decoder4to16_1_q15));
  or or_1 (point, decoder4to16_1_q10, decoder4to16_1_q11, decoder4to16_1_q12, decoder4to16_1_q13, decoder4to16_1_q14, decoder4to16_1_q15);
  or or_2 (F, decoder4to16_1_q0, decoder4to16_1_q4, decoder4to16_1_q5, decoder4to16_1_q6, decoder4to16_1_q8, decoder4to16_1_q9);
  or or_3 (G, decoder4to16_1_q2, decoder4to16_1_q3, decoder4to16_1_q4, decoder4to16_1_q5, decoder4to16_1_q6, decoder4to16_1_q8, decoder4to16_1_q9);
  or or_4 (A, decoder4to16_1_q0, decoder4to16_1_q2, decoder4to16_1_q3, decoder4to16_1_q5, decoder4to16_1_q6, decoder4to16_1_q7, decoder4to16_1_q8, decoder4to16_1_q9);
  or or_5 (B, decoder4to16_1_q0, decoder4to16_1_q1, decoder4to16_1_q2, decoder4to16_1_q3, decoder4to16_1_q4, decoder4to16_1_q7, decoder4to16_1_q8, decoder4to16_1_q9);
  or or_6 (C, decoder4to16_1_q0, decoder4to16_1_q1, decoder4to16_1_q3, decoder4to16_1_q4, decoder4to16_1_q5, decoder4to16_1_q6, decoder4to16_1_q7, decoder4to16_1_q8, decoder4to16_1_q9);
  or or_7 (D, decoder4to16_1_q0, decoder4to16_1_q2, decoder4to16_1_q3, decoder4to16_1_q5, decoder4to16_1_q6, decoder4to16_1_q8, decoder4to16_1_q9);
  or or_8 (E, decoder4to16_1_q0, decoder4to16_1_q2, decoder4to16_1_q6, decoder4to16_1_q8);
  _7_Segment_Display u_7_segment_display_1 (.g(G), .f(F), .a(A), .b(B), .e(E), .d(D), .c(C), .dp(point));
endmodule

module Decoder4to16 (
  input  A3,
  input  A2,
  input  A1,
  input  A0,
  input  EN,
  output Q0,
  output Q1,
  output Q2,
  output Q3,
  output Q4,
  output Q5,
  output Q6,
  output Q7,
  output Q8,
  output Q9,
  output Q10,
  output Q11,
  output Q12,
  output Q13,
  output Q14,
  output Q15
);

  wire and_1_out, and_2_out, not_1_out;

  not not_1 (not_1_out, A3);
  and and_1 (and_1_out, not_1_out, EN);
  and and_2 (and_2_out, A3, EN);
  Decoder3to8 decoder3to8_1 (
    .A2(A2), .A1(A1), .A0(A0), .EN(and_1_out), .Q0(Q0), .Q1(Q1), .Q2(Q2), .Q3(Q3), .Q4(Q4), .Q5(Q5), .Q6(Q6),
    .Q7(Q7));
  Decoder3to8 decoder3to8_2 (
    .A2(A2), .A1(A1), .A0(A0), .EN(and_2_out), .Q0(Q8), .Q1(Q9), .Q2(Q10), .Q3(Q11), .Q4(Q12), .Q5(Q13),
    .Q6(Q14), .Q7(Q15));
endmodule

module SevenSegDecoder_2 (
  input  A3,
  input  A2,
  input  A1,
  input  A0,
  input  EN,
  output A,
  output B,
  output C,
  output D,
  output E,
  output F,
  output G,
  output point
);

  wire decoder4to16_1_q0, decoder4to16_1_q1, decoder4to16_1_q2, decoder4to16_1_q3, decoder4to16_1_q4,
       decoder4to16_1_q5, decoder4to16_1_q6, decoder4to16_1_q7, decoder4to16_1_q8, decoder4to16_1_q9,
       decoder4to16_1_q10, decoder4to16_1_q11, decoder4to16_1_q12, decoder4to16_1_q13, decoder4to16_1_q14,
       decoder4to16_1_q15;

  Decoder4to16 decoder4to16_1 (
    .A3(A3), .A2(A2), .A1(A1), .A0(A0), .EN(EN), .Q0(decoder4to16_1_q0), .Q1(decoder4to16_1_q1),
    .Q2(decoder4to16_1_q2), .Q3(decoder4to16_1_q3), .Q4(decoder4to16_1_q4), .Q5(decoder4to16_1_q5),
    .Q6(decoder4to16_1_q6), .Q7(decoder4to16_1_q7), .Q8(decoder4to16_1_q8), .Q9(decoder4to16_1_q9),
    .Q10(decoder4to16_1_q10), .Q11(decoder4to16_1_q11), .Q12(decoder4to16_1_q12), .Q13(decoder4to16_1_q13),
    .Q14(decoder4to16_1_q14), .Q15(decoder4to16_1_q15));
  or or_1 (F, decoder4to16_1_q10, decoder4to16_1_q11, decoder4to16_1_q0, decoder4to16_1_q4, decoder4to16_1_q5, decoder4to16_1_q12, decoder4to16_1_q6, decoder4to16_1_q8, decoder4to16_1_q9, decoder4to16_1_q14, decoder4to16_1_q15);
  or or_2 (G, decoder4to16_1_q10, decoder4to16_1_q11, decoder4to16_1_q13, decoder4to16_1_q2, decoder4to16_1_q3, decoder4to16_1_q4, decoder4to16_1_q6, decoder4to16_1_q8, decoder4to16_1_q9, decoder4to16_1_q5, decoder4to16_1_q14, decoder4to16_1_q15);
  or or_3 (A, decoder4to16_1_q10, decoder4to16_1_q12, decoder4to16_1_q0, decoder4to16_1_q2, decoder4to16_1_q3, decoder4to16_1_q5, decoder4to16_1_q6, decoder4to16_1_q7, decoder4to16_1_q8, decoder4to16_1_q9, decoder4to16_1_q14, decoder4to16_1_q15);
  or or_4 (C, decoder4to16_1_q10, decoder4to16_1_q0, decoder4to16_1_q1, decoder4to16_1_q3, decoder4to16_1_q4, decoder4to16_1_q5, decoder4to16_1_q7, decoder4to16_1_q8, decoder4to16_1_q9, decoder4to16_1_q6, decoder4to16_1_q11, decoder4to16_1_q13);
  or or_5 (B, decoder4to16_1_q10, decoder4to16_1_q0, decoder4to16_1_q1, decoder4to16_1_q2, decoder4to16_1_q3, decoder4to16_1_q4, decoder4to16_1_q7, decoder4to16_1_q8, decoder4to16_1_q9, decoder4to16_1_q13);
  or or_6 (D, decoder4to16_1_q11, decoder4to16_1_q12, decoder4to16_1_q13, decoder4to16_1_q0, decoder4to16_1_q2, decoder4to16_1_q3, decoder4to16_1_q5, decoder4to16_1_q6, decoder4to16_1_q8, decoder4to16_1_q9, decoder4to16_1_q14);
  or or_7 (E, decoder4to16_1_q10, decoder4to16_1_q11, decoder4to16_1_q12, decoder4to16_1_q0, decoder4to16_1_q2, decoder4to16_1_q6, decoder4to16_1_q8, decoder4to16_1_q13, decoder4to16_1_q14, decoder4to16_1_q15);
  _7_Segment_Display u_7_segment_display_1 (.g(G), .f(F), .a(A), .b(B), .e(E), .d(D), .c(C), .dp(1'b0));

  assign point = 1'b0;
endmodule

module Encoder16to4 (
  input  A15,
  input  A14,
  input  A13,
  input  A12,
  input  A11,
  input  A10,
  input  A9,
  input  A8,
  input  A7,
  input  A6,
  input  A5,
  input  A4,
  input  A3,
  input  A2,
  input  A1,
  input  A0,
  output Q3,
  output Q2,
  output Q1,
  output Q0
);

  or or_1 (Q3, A15, A14, A13, A12, A11, A10, A9, A8);
  or or_2 (Q1, A15, A14, A11, A10, A7, A6, A3, A2);
  or or_3 (Q2, A15, A14, A13, A12, A7, A6, A5, A4);
  or or_4 (Q0, A15, A13, A11, A9, A7, A5, A3, A1);
endmodule

module EncodertoSevenSeg (
  input  A15,
  input  A14,
  input  A13,
  input  A12,
  input  A11,
  input  A10,
  input  A9,
  input  A8,
  input  A7,
  input  A6,
  input  A5,
  input  A4,
  input  A3,
  input  A2,
  input  A1,
  input  A0
);

  wire encoder16to4_1_q0, encoder16to4_1_q1, encoder16to4_1_q2, encoder16to4_1_q3, sevensegdecoder_2_1_a,
       sevensegdecoder_2_1_b, sevensegdecoder_2_1_c, sevensegdecoder_2_1_d, sevensegdecoder_2_1_e,
       sevensegdecoder_2_1_f, sevensegdecoder_2_1_g, sevensegdecoder_2_1_point;

  Encoder16to4 encoder16to4_1 (
    .A15(A15), .A14(A14), .A13(A13), .A12(A12), .A11(A11), .A10(A10), .A9(A9), .A8(A8), .A7(A7), .A6(A6),
    .A5(A5), .A4(A4), .A3(A3), .A2(A2), .A1(A1), .A0(A0), .Q3(encoder16to4_1_q3), .Q2(encoder16to4_1_q2),
    .Q1(encoder16to4_1_q1), .Q0(encoder16to4_1_q0));
  SevenSegDecoder_2 sevensegdecoder_2_1 (
    .A3(encoder16to4_1_q3), .A2(encoder16to4_1_q2), .A1(encoder16to4_1_q1), .A0(encoder16to4_1_q0),
    .EN(1'b1), .A(sevensegdecoder_2_1_a), .B(sevensegdecoder_2_1_b), .C(sevensegdecoder_2_1_c),
    .D(sevensegdecoder_2_1_d), .E(sevensegdecoder_2_1_e), .F(sevensegdecoder_2_1_f),
    .G(sevensegdecoder_2_1_g), .point(sevensegdecoder_2_1_point));
  _7_Segment_Display u_7_segment_display_1 (
    .g(sevensegdecoder_2_1_g), .f(sevensegdecoder_2_1_f), .a(sevensegdecoder_2_1_a),
    .b(sevensegdecoder_2_1_b), .e(sevensegdecoder_2_1_e), .d(sevensegdecoder_2_1_d),
    .c(sevensegdecoder_2_1_c), .dp(sevensegdecoder_2_1_point));
endmodule

module PriorityEncoder4to2 (
  input  A3,
  input  A2,
  input  A1,
  input  A0,
  input  S,
  output Y1,
  output Y0,
  output YS,
  output YEX
);

  wire and_1_out, not_1_out, not_2_out, not_3_out, or_1_out, or_2_out;

  not not_1 (not_1_out, A2);
  not not_2 (not_2_out, S);
  and and_1 (and_1_out, not_1_out, A1);
  or or_1 (or_1_out, A3, A2);
  or or_2 (or_2_out, A3, and_1_out);
  not not_3 (not_3_out, YS);
  and and_2 (Y1, or_1_out, S);
  and and_3 (Y0, or_2_out, S);
  nor nor_1 (YS, A3, A2, A1, A0, not_2_out);
  and and_4 (YEX, not_3_out, S);
endmodule

module PriorityEncoder8to3 (
  input  A7,
  input  A6,
  input  A5,
  input  A4,
  input  A3,
  input  A2,
  input  A1,
  input  A0,
  input  S,
  output Y2,
  output Y1,
  output Y0,
  output YS,
  output YEX
);

  wire priorityencoder4to2_1_y0, priorityencoder4to2_1_y1, priorityencoder4to2_1_ys,
       priorityencoder4to2_2_y0, priorityencoder4to2_2_y1, priorityencoder4to2_2_yex;

  PriorityEncoder4to2 priorityencoder4to2_1 (
    .A3(A7), .A2(A6), .A1(A5), .A0(A4), .S(S), .Y1(priorityencoder4to2_1_y1), .Y0(priorityencoder4to2_1_y0),
    .YS(priorityencoder4to2_1_ys), .YEX(Y2));
  PriorityEncoder4to2 priorityencoder4to2_2 (
    .A3(A3), .A2(A2), .A1(A1), .A0(A0), .S(priorityencoder4to2_1_ys), .Y1(priorityencoder4to2_2_y1),
    .Y0(priorityencoder4to2_2_y0), .YS(YS), .YEX(priorityencoder4to2_2_yex));
  or or_1 (Y1, priorityencoder4to2_1_y1, priorityencoder4to2_2_y1);
  or or_2 (Y0, priorityencoder4to2_1_y0, priorityencoder4to2_2_y0);
  or or_3 (YEX, Y2, priorityencoder4to2_2_yex);
endmodule

module PriorityEncoder16to4 (
  input  A15,
  input  A14,
  input  A13,
  input  A12,
  input  A11,
  input  A10,
  input  A9,
  input  A8,
  input  A7,
  input  A6,
  input  A5,
  input  A4,
  input  A3,
  input  A2,
  input  A1,
  input  A0,
  input  S,
  output Y3,
  output Y2,
  output Y1,
  output Y0,
  output YS,
  output YEX
);

  wire priorityencoder8to3_1_y0, priorityencoder8to3_1_y1, priorityencoder8to3_1_y2,
       priorityencoder8to3_1_ys, priorityencoder8to3_2_y0, priorityencoder8to3_2_y1,
       priorityencoder8to3_2_y2, priorityencoder8to3_2_yex;

  PriorityEncoder8to3 priorityencoder8to3_1 (
    .A7(A15), .A6(A14), .A5(A13), .A4(A12), .A3(A11), .A2(A10), .A1(A9), .A0(A8), .S(S),
    .Y2(priorityencoder8to3_1_y2), .Y1(priorityencoder8to3_1_y1), .Y0(priorityencoder8to3_1_y0),
    .YS(priorityencoder8to3_1_ys), .YEX(Y3));
  PriorityEncoder8to3 priorityencoder8to3_2 (
    .A7(A7), .A6(A6), .A5(A5), .A4(A4), .A3(A3), .A2(A2), .A1(A1), .A0(A0), .S(priorityencoder8to3_1_ys),
    .Y2(priorityencoder8to3_2_y2), .Y1(priorityencoder8to3_2_y1), .Y0(priorityencoder8to3_2_y0), .YS(YS),
    .YEX(priorityencoder8to3_2_yex));
  or or_1 (Y2, priorityencoder8to3_1_y2, priorityencoder8to3_2_y2);
  or or_2 (Y1, priorityencoder8to3_1_y1, priorityencoder8to3_2_y1);
  or or_3 (Y0, priorityencoder8to3_1_y0, priorityencoder8to3_2_y0);
  or or_4 (YEX, Y3, priorityencoder8to3_2_yex);
endmodule

module PriorityEncodertoSevenSeg (
  input  A15,
  input  A14,
  input  A13,
  input  A12,
  input  A11,
  input  A10,
  input  A9,
  input  A8,
  input  A7,
  input  A6,
  input  A5,
  input  A4,
  input  A3,
  input  A2,
  input  A1,
  input  A0,
  input  S,
  output out_18
);

  wire priorityencoder16to4_1_y0, priorityencoder16to4_1_y1, priorityencoder16to4_1_y2,
       priorityencoder16to4_1_y3, priorityencoder16to4_1_yex, sevensegdecoder_2_1_a, sevensegdecoder_2_1_b,
       sevensegdecoder_2_1_c, sevensegdecoder_2_1_d, sevensegdecoder_2_1_e, sevensegdecoder_2_1_f,
       sevensegdecoder_2_1_g, sevensegdecoder_2_1_point;

  PriorityEncoder16to4 priorityencoder16to4_1 (
    .A15(A15), .A14(A14), .A13(A13), .A12(A12), .A11(A11), .A10(A10), .A9(A9), .A8(A8), .A7(A7), .A6(A6),
    .A5(A5), .A4(A4), .A3(A3), .A2(A2), .A1(A1), .A0(A0), .S(S), .Y3(priorityencoder16to4_1_y3),
    .Y2(priorityencoder16to4_1_y2), .Y1(priorityencoder16to4_1_y1), .Y0(priorityencoder16to4_1_y0),
    .YS(out_18), .YEX(priorityencoder16to4_1_yex));
  SevenSegDecoder_2 sevensegdecoder_2_1 (
    .A3(priorityencoder16to4_1_y3), .A2(priorityencoder16to4_1_y2), .A1(priorityencoder16to4_1_y1),
    .A0(priorityencoder16to4_1_y0), .EN(priorityencoder16to4_1_yex), .A(sevensegdecoder_2_1_a),
    .B(sevensegdecoder_2_1_b), .C(sevensegdecoder_2_1_c), .D(sevensegdecoder_2_1_d),
    .E(sevensegdecoder_2_1_e), .F(sevensegdecoder_2_1_f), .G(sevensegdecoder_2_1_g),
    .point(sevensegdecoder_2_1_point));
  _7_Segment_Display u_7_segment_display_1 (
    .g(sevensegdecoder_2_1_g), .f(sevensegdecoder_2_1_f), .a(sevensegdecoder_2_1_a),
    .b(sevensegdecoder_2_1_b), .e(sevensegdecoder_2_1_e), .d(sevensegdecoder_2_1_d),
    .c(sevensegdecoder_2_1_c), .dp(sevensegdecoder_2_1_point));
endmodule

module Mux2to1 (
  input  S,
  input  D0,
  input  D1,
  output Y
);

  wire and_1_out, and_2_out, not_1_out;

  not not_1 (not_1_out, S);
  and and_1 (and_1_out, D0, not_1_out);
  and and_2 (and_2_out, D1, S);
  or or_1 (Y, and_1_out, and_2_out);
endmodule

module Mux4to1_3bit (
  input  [2:0] D0,
  input  [2:0] D1,
  input  [2:0] D2,
  input  [2:0] D3,
  input  S1,
  input  S0,
  output [2:0] Y
);

  wire and_1_out, and_2_out, and_3_out, and_4_out, and_5_out, and_6_out, and_7_out, and_8_out, and_9_out,
       and_10_out, and_11_out, and_12_out, decoder2to4_1_q0, decoder2to4_1_q1, decoder2to4_1_q2,
       decoder2to4_1_q3;

  and and_1 (and_1_out, D0[0], decoder2to4_1_q0);
  and and_2 (and_2_out, D1[0], decoder2to4_1_q1);
  and and_3 (and_3_out, D2[0], decoder2to4_1_q2);
  and and_4 (and_4_out, D3[0], decoder2to4_1_q3);
  or or_1 (Y[0], and_1_out, and_2_out, and_3_out, and_4_out);
  and and_5 (and_5_out, D0[1], decoder2to4_1_q0);
  and and_6 (and_6_out, D1[1], decoder2to4_1_q1);
  and and_7 (and_7_out, D2[1], decoder2to4_1_q2);
  and and_8 (and_8_out, D3[1], decoder2to4_1_q3);
  Decoder2to4 decoder2to4_1 (
    .A0(S1), .A1(S0), .EN(1'b1), .Q0(decoder2to4_1_q0), .Q1(decoder2to4_1_q1), .Q2(decoder2to4_1_q2),
    .Q3(decoder2to4_1_q3));
  or or_2 (Y[1], and_5_out, and_6_out, and_7_out, and_8_out);
  and and_9 (and_9_out, D0[2], decoder2to4_1_q0);
  and and_10 (and_10_out, D1[2], decoder2to4_1_q1);
  and and_11 (and_11_out, D2[2], decoder2to4_1_q2);
  and and_12 (and_12_out, D3[2], decoder2to4_1_q3);
  or or_3 (Y[2], and_9_out, and_10_out, and_11_out, and_12_out);
endmodule

module SevenSegDecHexSwitch (
  input  A3,
  input  A2,
  input  A1,
  input  A0,
  input  S
);

  wire mux2to1_1_y, mux2to1_2_y, mux2to1_3_y, mux2to1_4_y, mux2to1_5_y, mux2to1_6_y, mux2to1_7_y,
       mux2to1_8_y, sevensegdecoder_1_1_a, sevensegdecoder_1_1_b, sevensegdecoder_1_1_c,
       sevensegdecoder_1_1_d, sevensegdecoder_1_1_e, sevensegdecoder_1_1_f, sevensegdecoder_1_1_g,
       sevensegdecoder_1_1_point, sevensegdecoder_2_1_a, sevensegdecoder_2_1_b, sevensegdecoder_2_1_c,
       sevensegdecoder_2_1_d, sevensegdecoder_2_1_e, sevensegdecoder_2_1_f, sevensegdecoder_2_1_g,
       sevensegdecoder_2_1_point;

  SevenSegDecoder_1 sevensegdecoder_1_1 (
    .A0(A3), .A1(A2), .A2(A1), .A3(A0), .EN(1'b1), .A(sevensegdecoder_1_1_a), .B(sevensegdecoder_1_1_b),
    .C(sevensegdecoder_1_1_c), .D(sevensegdecoder_1_1_d), .E(sevensegdecoder_1_1_e),
    .F(sevensegdecoder_1_1_f), .G(sevensegdecoder_1_1_g), .point(sevensegdecoder_1_1_point));
  SevenSegDecoder_2 sevensegdecoder_2_1 (
    .A3(A3), .A2(A2), .A1(A1), .A0(A0), .EN(1'b1), .A(sevensegdecoder_2_1_a), .B(sevensegdecoder_2_1_b),
    .C(sevensegdecoder_2_1_c), .D(sevensegdecoder_2_1_d), .E(sevensegdecoder_2_1_e),
    .F(sevensegdecoder_2_1_f), .G(sevensegdecoder_2_1_g), .point(sevensegdecoder_2_1_point));
  Mux2to1 mux2to1_1 (.S(S), .D0(sevensegdecoder_1_1_a), .D1(sevensegdecoder_2_1_a), .Y(mux2to1_1_y));
  Mux2to1 mux2to1_2 (.S(S), .D0(sevensegdecoder_1_1_b), .D1(sevensegdecoder_2_1_b), .Y(mux2to1_2_y));
  Mux2to1 mux2to1_3 (.S(S), .D0(sevensegdecoder_1_1_c), .D1(sevensegdecoder_2_1_c), .Y(mux2to1_3_y));
  Mux2to1 mux2to1_4 (.S(S), .D0(sevensegdecoder_1_1_d), .D1(sevensegdecoder_2_1_d), .Y(mux2to1_4_y));
  Mux2to1 mux2to1_5 (.S(S), .D0(sevensegdecoder_1_1_e), .D1(sevensegdecoder_2_1_e), .Y(mux2to1_5_y));
  Mux2to1 mux2to1_6 (.S(S), .D0(sevensegdecoder_1_1_f), .D1(sevensegdecoder_2_1_f), .Y(mux2to1_6_y));
  Mux2to1 mux2to1_7 (.S(S), .D0(sevensegdecoder_1_1_g), .D1(sevensegdecoder_2_1_g), .Y(mux2to1_7_y));
  Mux2to1 mux2to1_8 (.S(S), .D0(sevensegdecoder_1_1_point), .D1(sevensegdecoder_2_1_point), .Y(mux2to1_8_y));
  _7_Segment_Display u_7_segment_display_1 (
    .g(mux2to1_7_y), .f(mux2to1_6_y), .a(mux2to1_1_y), .b(mux2to1_2_y), .e(mux2to1_5_y), .d(mux2to1_4_y),
    .c(mux2to1_3_y), .dp(mux2to1_8_y));
endmodule

module Comparator4bit (
  input  [3:0] A,
  input  [3:0] B
);

  wire nor_1_out, xor_1_out, xor_2_out, xor_3_out, xor_4_out;

  xor xor_1 (xor_1_out, A[0], B[0]);
  xor xor_2 (xor_2_out, A[1], B[1]);
  xor xor_3 (xor_3_out, A[2], B[2]);
  xor xor_4 (xor_4_out, A[3], B[3]);
  nor nor_1 (nor_1_out, xor_1_out, xor_2_out, xor_3_out, xor_4_out);
  LED led_1 (.in(nor_1_out));
endmodule

module Adder1bit (
  input  A,
  input  B,
  input  Cin,
  output S,
  output Cout
);

  wire and_1_out, and_2_out, xor_1_out;

  and and_1 (and_1_out, A, B);
  xor xor_1 (xor_1_out, A, B);
  xor xor_2 (S, xor_1_out, Cin);
  and and_2 (and_2_out, Cin, xor_1_out);
  or or_1 (Cout, and_1_out, and_2_out);
endmodule

module Halfadder (
  input  A,
  input  B,
  output S,
  output Cout
);

  xor xor_1 (S, A, B);
  and and_1 (Cout, A, B);
endmodule

module Adder1bit_2 (
  input  A,
  input  B,
  input  Cin,
  output S,
  output Cout
);

  wire halfadder_1_cout, halfadder_1_s, halfadder_2_cout;

  Halfadder halfadder_1 (.A(A), .B(B), .S(halfadder_1_s), .Cout(halfadder_1_cout));
  Halfadder halfadder_2 (.A(halfadder_1_s), .B(Cin), .S(S), .Cout(halfadder_2_cout));
  or or_1 (Cout, halfadder_1_cout, halfadder_2_cout);
endmodule

module Adder4bit (
  input  Cin,
  input  A0,
  input  A1,
  input  A2,
  input  A3,
  input  B0,
  input  B1,
  input  B2,
  input  B3,
  output Y0,
  output Y1,
  output Y2,
  output Y3,
  output Cout
);

  wire adder1bit_2_1_cout, adder1bit_2_2_cout, adder1bit_2_3_cout;

  Adder1bit_2 adder1bit_2_1 (.A(A0), .B(B0), .Cin(Cin), .S(Y0), .Cout(adder1bit_2_1_cout));
  Adder1bit_2 adder1bit_2_2 (.A(A1), .B(B1), .Cin(adder1bit_2_1_cout), .S(Y1), .Cout(adder1bit_2_2_cout));
  Adder1bit_2 adder1bit_2_3 (.A(A2), .B(B2), .Cin(adder1bit_2_2_cout), .S(Y2), .Cout(adder1bit_2_3_cout));
  Adder1bit_2 adder1bit_2_4 (.A(A3), .B(B3), .Cin(adder1bit_2_3_cout), .S(Y3), .Cout(Cout));
endmodule

module SRlatch (
  input  R,
  input  EN,
  input  S,
  output Q,
  output Q_bar
);

  wire and_1_out, and_2_out;

  and and_1 (and_1_out, R, EN);
  and and_2 (and_2_out, EN, S);
  nor nor_1 (Q, and_1_out, Q_bar);
  nor nor_2 (Q_bar, Q, and_2_out);
endmodule

module Dlatch_r (
  input  D,
  input  WE,
  input  R,
  output Q,
  output Q_bar
);

  wire and_1_out, and_2_out, not_1_out, or_1_out;

  not not_1 (not_1_out, D);
  and and_1 (and_1_out, not_1_out, WE);
  and and_2 (and_2_out, WE, D);
  or or_1 (or_1_out, and_1_out, R);
  SRlatch srlatch_1 (.R(or_1_out), .EN(1'b1), .S(and_2_out), .Q(Q), .Q_bar(Q_bar));
endmodule

module Dlatch (
  input  D,
  input  WE,
  output Q,
  output Q_bar
);

  wire and_1_out, and_2_out, not_1_out;

  not not_1 (not_1_out, D);
  and and_1 (and_1_out, not_1_out, WE);
  and and_2 (and_2_out, WE, D);
  SRlatch srlatch_1 (.R(and_1_out), .EN(1'b1), .S(and_2_out), .Q(Q), .Q_bar(Q_bar));
endmodule

module Dflipflop_r (
  input  D,
  input  R,
  output Q,
  output Q_bar
);

  wire and_1_out, clock_1_out, dlatch_1_q, not_1_out, not_2_out;

  Clock clock_1 (.out(clock_1_out));
  not not_1 (not_1_out, clock_1_out);
  not not_2 (not_2_out, R);
  Dlatch dlatch_1 (.D(D), .WE(not_1_out), .Q(dlatch_1_q));  // open: Q_bar
  and and_1 (and_1_out, dlatch_1_q, not_2_out);
  Dlatch dlatch_2 (.D(and_1_out), .WE(clock_1_out), .Q(Q), .Q_bar(Q_bar));
endmodule

module Dflipflop_en (
  input  D,
  input  EN,
  input  CLK,
  output out_4,
  output out_5
);

  wire and_1_out, and_2_out, not_1_out, or_1_out;

  not not_1 (not_1_out, EN);
  and and_1 (and_1_out, D, EN);
  and and_2 (and_2_out, not_1_out, out_4);
  or or_1 (or_1_out, and_1_out, and_2_out);
  Dflipflop dflipflop_1 (.D(or_1_out), .CLK(CLK), .Q(out_4), .Q_bar(out_5));
endmodule

module Dflipflop (
  input  D,
  input  CLK,
  output Q,
  output Q_bar
);

  wire dlatch_1_q, not_1_out;

  not not_1 (not_1_out, CLK);
  Dlatch dlatch_1 (.D(D), .WE(not_1_out), .Q(dlatch_1_q));  // open: Q_bar
  Dlatch dlatch_2 (.D(dlatch_1_q), .WE(CLK), .Q(Q), .Q_bar(Q_bar));
endmodule

module register4bit (
  input  D0,
  input  D1,
  input  D2,
  input  D3,
  input  EN,
  input  CLK,
  input  R,
  output Q0,
  output Q1,
  output Q2,
  output Q3
);

  wire and_1_out, and_2_out, and_3_out, and_4_out, not_1_out, or_1_out;

  not not_1 (not_1_out, R);
  and and_1 (and_1_out, D0, not_1_out);
  and and_2 (and_2_out, D1, not_1_out);
  and and_3 (and_3_out, D2, not_1_out);
  and and_4 (and_4_out, D3, not_1_out);
  or or_1 (or_1_out, EN, R);
  Dflipflop_en dflipflop_en_1 (.D(and_1_out), .EN(or_1_out), .CLK(CLK), .out_4(Q0));  // open: out_5
  Dflipflop_en dflipflop_en_2 (.D(and_2_out), .EN(or_1_out), .CLK(CLK), .out_4(Q1));  // open: out_5
  Dflipflop_en dflipflop_en_3 (.D(and_3_out), .EN(or_1_out), .CLK(CLK), .out_4(Q2));  // open: out_5
  Dflipflop_en dflipflop_en_4 (.D(and_4_out), .EN(or_1_out), .CLK(CLK), .out_4(Q3));  // open: out_5
endmodule

module registerSevenSeg (
  input  D0,
  input  D1,
  input  D2,
  input  D3,
  input  EN,
  input  CLK,
  input  R
);

  wire register4bit_1_q0, register4bit_1_q1, register4bit_1_q2, register4bit_1_q3, sevensegdecoder_2_1_a,
       sevensegdecoder_2_1_b, sevensegdecoder_2_1_c, sevensegdecoder_2_1_d, sevensegdecoder_2_1_e,
       sevensegdecoder_2_1_f, sevensegdecoder_2_1_g, sevensegdecoder_2_1_point;

  register4bit register4bit_1 (
    .D0(D0), .D1(D1), .D2(D2), .D3(D3), .EN(EN), .CLK(CLK), .R(R), .Q0(register4bit_1_q0),
    .Q1(register4bit_1_q1), .Q2(register4bit_1_q2), .Q3(register4bit_1_q3));
  SevenSegDecoder_2 sevensegdecoder_2_1 (
    .A3(register4bit_1_q0), .A2(register4bit_1_q1), .A1(register4bit_1_q2), .A0(register4bit_1_q3),
    .EN(1'b1), .A(sevensegdecoder_2_1_a), .B(sevensegdecoder_2_1_b), .C(sevensegdecoder_2_1_c),
    .D(sevensegdecoder_2_1_d), .E(sevensegdecoder_2_1_e), .F(sevensegdecoder_2_1_f),
    .G(sevensegdecoder_2_1_g), .point(sevensegdecoder_2_1_point));
  _7_Segment_Display u_7_segment_display_1 (
    .g(sevensegdecoder_2_1_g), .f(sevensegdecoder_2_1_f), .a(sevensegdecoder_2_1_a),
    .b(sevensegdecoder_2_1_b), .e(sevensegdecoder_2_1_e), .d(sevensegdecoder_2_1_d),
    .c(sevensegdecoder_2_1_c), .dp(sevensegdecoder_2_1_point));
endmodule

module counter_1 (
  input  in_1,
  input  in_2,
  output out_3,
  output out_4,
  output out_5,
  output out_6
);

  wire adder4bit_1_y0, adder4bit_1_y1, adder4bit_1_y2, adder4bit_1_y3;

  register4bit register4bit_1 (
    .D0(adder4bit_1_y0), .D1(adder4bit_1_y1), .D2(adder4bit_1_y2), .D3(adder4bit_1_y3), .EN(1'b1),
    .CLK(in_1), .R(in_2), .Q0(out_3), .Q1(out_4), .Q2(out_5), .Q3(out_6));
  Adder4bit adder4bit_1 (
    .Cin(1'b0), .A0(out_3), .A1(out_4), .A2(out_5), .A3(out_6), .B0(1'b1), .B1(1'b0), .B2(1'b0), .B3(1'b0),
    .Y0(adder4bit_1_y0), .Y1(adder4bit_1_y1), .Y2(adder4bit_1_y2), .Y3(adder4bit_1_y3));  // open: Cout
endmodule

module arrayadd (
  input  CLK,
  input  RN,
  input  RS,
  output N0,
  output N1,
  output N2,
  output N3,
  output S0,
  output S1,
  output S2,
  output S3,
  output S4,
  output S5,
  output S6,
  output S7
);

  wire adder4bit_1_y0, adder4bit_1_y1, adder4bit_1_y2, adder4bit_1_y3, adder8bit_1_q0, adder8bit_1_q1,
       adder8bit_1_q2, adder8bit_1_q3, adder8bit_1_q4, adder8bit_1_q5, adder8bit_1_q6, adder8bit_1_q7,
       comparator_1_eq, comparator_1_lt, or_1_out;

  register4bit register4bit_1 (
    .D0(adder4bit_1_y0), .D1(adder4bit_1_y1), .D2(adder4bit_1_y2), .D3(adder4bit_1_y3), .EN(or_1_out),
    .CLK(CLK), .R(RN), .Q0(N0), .Q1(N1), .Q2(N2), .Q3(N3));
  Adder4bit adder4bit_1 (
    .Cin(1'b0), .A0(N0), .A1(N1), .A2(N2), .A3(N3), .B0(1'b1), .B1(1'b0), .B2(1'b0), .B3(1'b0),
    .Y0(adder4bit_1_y0), .Y1(adder4bit_1_y1), .Y2(adder4bit_1_y2), .Y3(adder4bit_1_y3));  // open: Cout
  Adder8bit adder8bit_1 (
    .Cin(1'b0), .A0(N0), .A1(N1), .A2(N2), .A3(N3), .A4(1'b0), .A5(1'b0), .A6(1'b0), .A7(1'b0), .B0(S0),
    .B1(S1), .B2(S2), .B3(S3), .B4(S4), .B5(S5), .B6(S6), .B7(S7), .Q0(adder8bit_1_q0), .Q1(adder8bit_1_q1),
    .Q2(adder8bit_1_q2), .Q3(adder8bit_1_q3), .Q4(adder8bit_1_q4), .Q5(adder8bit_1_q5), .Q6(adder8bit_1_q6),
    .Q7(adder8bit_1_q7));  // open: Cout
  Comparator #(.mode("unsigned"), .width(4)) comparator_1 (
    .a({N3, N2, N1, N0}), .b(4'b1010), .eq(comparator_1_eq), .lt(comparator_1_lt));  // open: gt
  or or_1 (or_1_out, comparator_1_eq, comparator_1_lt);
  register8bit register8bit_1 (
    .D0(adder8bit_1_q0), .D1(adder8bit_1_q1), .D2(adder8bit_1_q2), .D3(adder8bit_1_q3), .D4(adder8bit_1_q4),
    .D5(adder8bit_1_q5), .D6(adder8bit_1_q6), .D7(adder8bit_1_q7), .EN(or_1_out), .CLK(CLK), .R(RS), .Q0(S0),
    .Q1(S1), .Q2(S2), .Q3(S3), .Q4(S4), .Q5(S5), .Q6(S6), .Q7(S7));
endmodule

module register8bit (
  input  D0,
  input  D1,
  input  D2,
  input  D3,
  input  D4,
  input  D5,
  input  D6,
  input  D7,
  input  EN,
  input  CLK,
  input  R,
  output Q0,
  output Q1,
  output Q2,
  output Q3,
  output Q4,
  output Q5,
  output Q6,
  output Q7
);

  wire and_1_out, and_2_out, and_3_out, and_4_out, and_5_out, and_6_out, and_7_out, and_8_out, not_1_out,
       or_1_out;

  not not_1 (not_1_out, R);
  and and_1 (and_1_out, D0, not_1_out);
  and and_2 (and_2_out, D1, not_1_out);
  and and_3 (and_3_out, D2, not_1_out);
  and and_4 (and_4_out, D3, not_1_out);
  and and_5 (and_5_out, D4, not_1_out);
  and and_6 (and_6_out, D5, not_1_out);
  and and_7 (and_7_out, D6, not_1_out);
  and and_8 (and_8_out, D7, not_1_out);
  or or_1 (or_1_out, EN, R);
  Dflipflop_en dflipflop_en_1 (.D(and_1_out), .EN(or_1_out), .CLK(CLK), .out_4(Q0));  // open: out_5
  Dflipflop_en dflipflop_en_2 (.D(and_2_out), .EN(or_1_out), .CLK(CLK), .out_4(Q1));  // open: out_5
  Dflipflop_en dflipflop_en_3 (.D(and_3_out), .EN(or_1_out), .CLK(CLK), .out_4(Q2));  // open: out_5
  Dflipflop_en dflipflop_en_4 (.D(and_4_out), .EN(or_1_out), .CLK(CLK), .out_4(Q3));  // open: out_5
  Dflipflop_en dflipflop_en_5 (.D(and_5_out), .EN(or_1_out), .CLK(CLK), .out_4(Q4));  // open: out_5
  Dflipflop_en dflipflop_en_6 (.D(and_6_out), .EN(or_1_out), .CLK(CLK), .out_4(Q5));  // open: out_5
  Dflipflop_en dflipflop_en_7 (.D(and_7_out), .EN(or_1_out), .CLK(CLK), .out_4(Q6));  // open: out_5
  Dflipflop_en dflipflop_en_8 (.D(and_8_out), .EN(or_1_out), .CLK(CLK), .out_4(Q7));  // open: out_5
endmodule

module Adder8bit (
  input  Cin,
  input  A0,
  input  A1,
  input  A2,
  input  A3,
  input  A4,
  input  A5,
  input  A6,
  input  A7,
  input  B0,
  input  B1,
  input  B2,
  input  B3,
  input  B4,
  input  B5,
  input  B6,
  input  B7,
  output Q0,
  output Q1,
  output Q2,
  output Q3,
  output Q4,
  output Q5,
  output Q6,
  output Q7,
  output Cout
);

  wire adder4bit_1_cout;

  Adder4bit adder4bit_1 (
    .Cin(Cin), .A0(A0), .A1(A1), .A2(A2), .A3(A3), .B0(B0), .B1(B1), .B2(B2), .B3(B3), .Y0(Q0), .Y1(Q1),
    .Y2(Q2), .Y3(Q3), .Cout(adder4bit_1_cout));
  Adder4bit adder4bit_2 (
    .Cin(adder4bit_1_cout), .A0(A4), .A1(A5), .A2(A6), .A3(A7), .B0(B4), .B1(B5), .B2(B6), .B3(B7), .Y0(Q4),
    .Y1(Q5), .Y2(Q6), .Y3(Q7), .Cout(Cout));
endmodule

module time_1 (
  input  R,
  output Q0,
  output out_3,
  output Q1,
  output out_5,
  output Q2,
  output out_7,
  output Q3,
  output out_9,
  output Q4,
  output out_11,
  output Q5,
  output out_13,
  output Q6,
  output out_15,
  output Q7,
  output out_17
);

  wire adder8bit_1_q0, adder8bit_1_q1, adder8bit_1_q2, adder8bit_1_q3, adder8bit_1_q4, adder8bit_1_q5,
       adder8bit_1_q6, adder8bit_1_q7, adder8bit_2_q0, adder8bit_2_q1, adder8bit_2_q2, adder8bit_2_q3,
       adder8bit_2_q4, adder8bit_2_q5, adder8bit_2_q6, adder8bit_2_q7, and_1_out, CLK_out, comparator_1_eq,
       comparator_2_eq, or_1_out, or_2_out;

  Clock CLK (.out(CLK_out));
  or or_1 (or_1_out, R, comparator_1_eq);
  register8bit register8bit_1 (
    .D0(adder8bit_1_q0), .D1(adder8bit_1_q1), .D2(adder8bit_1_q2), .D3(adder8bit_1_q3), .D4(adder8bit_1_q4),
    .D5(adder8bit_1_q5), .D6(adder8bit_1_q6), .D7(adder8bit_1_q7), .EN(1'b1), .CLK(CLK_out), .R(or_1_out),
    .Q0(Q0), .Q1(Q1), .Q2(Q2), .Q3(Q3), .Q4(Q4), .Q5(Q5), .Q6(Q6), .Q7(Q7));
  Adder8bit adder8bit_1 (
    .Cin(1'b0), .A0(Q0), .A1(Q1), .A2(Q2), .A3(Q3), .A4(Q4), .A5(Q5), .A6(Q6), .A7(Q7), .B0(1'b1), .B1(1'b0),
    .B2(1'b0), .B3(1'b0), .B4(1'b0), .B5(1'b0), .B6(1'b0), .B7(1'b0), .Q0(adder8bit_1_q0),
    .Q1(adder8bit_1_q1), .Q2(adder8bit_1_q2), .Q3(adder8bit_1_q3), .Q4(adder8bit_1_q4), .Q5(adder8bit_1_q5),
    .Q6(adder8bit_1_q6), .Q7(adder8bit_1_q7));  // open: Cout
  Comparator #(.mode("unsigned")) comparator_1 (
    .a({Q7, Q6, Q5, Q4, Q3, Q2, Q1, Q0}), .b(8'h3b), .eq(comparator_1_eq));  // open: gt, lt
  and and_1 (and_1_out, comparator_1_eq, comparator_2_eq);
  or or_2 (or_2_out, and_1_out, R);
  register8bit register8bit_2 (
    .D0(adder8bit_2_q0), .D1(adder8bit_2_q1), .D2(adder8bit_2_q2), .D3(adder8bit_2_q3), .D4(adder8bit_2_q4),
    .D5(adder8bit_2_q5), .D6(adder8bit_2_q6), .D7(adder8bit_2_q7), .EN(comparator_1_eq), .CLK(CLK_out),
    .R(or_2_out), .Q0(out_3), .Q1(out_5), .Q2(out_7), .Q3(out_9), .Q4(out_11), .Q5(out_13), .Q6(out_15),
    .Q7(out_17));
  Adder8bit adder8bit_2 (
    .Cin(1'b0), .A0(out_3), .A1(out_5), .A2(out_7), .A3(out_9), .A4(out_11), .A5(out_13), .A6(out_15),
    .A7(out_17), .B0(1'b1), .B1(1'b0), .B2(1'b0), .B3(1'b0), .B4(1'b0), .B5(1'b0), .B6(1'b0), .B7(1'b0),
    .Q0(adder8bit_2_q0), .Q1(adder8bit_2_q1), .Q2(adder8bit_2_q2), .Q3(adder8bit_2_q3), .Q4(adder8bit_2_q4),
    .Q5(adder8bit_2_q5), .Q6(adder8bit_2_q6), .Q7(adder8bit_2_q7));  // open: Cout
  Comparator #(.mode("unsigned")) comparator_2 (
    .a({out_17, out_15, out_13, out_11, out_9, out_7, out_5, out_3}), .b(8'h3b), .eq(comparator_2_eq));  // open: gt, lt
endmodule

module timeclock (
  input  R
);

  wire adder4bit_1_y0, adder4bit_1_y1, adder4bit_1_y2, adder4bit_1_y3, adder4bit_2_y0, adder4bit_2_y1,
       adder4bit_2_y2, adder4bit_2_y3, adder4bit_3_y0, adder4bit_3_y1, adder4bit_3_y2, adder4bit_3_y3,
       adder4bit_4_y0, adder4bit_4_y1, adder4bit_4_y2, adder4bit_4_y3, adder4bit_5_y0, adder4bit_5_y1,
       adder4bit_5_y2, adder4bit_5_y3, adder4bit_6_y0, adder4bit_6_y1, adder4bit_6_y2, adder4bit_6_y3,
       and_1_out, and_2_out, and_3_out, and_4_out, and_5_out, and_6_out, CLK_out, comparator_1_eq,
       comparator_2_eq, comparator_3_eq, comparator_4_eq, comparator_5_eq, comparator_6_eq, comparator_7_eq,
       or_1_out, or_2_out, or_3_out, or_4_out, or_5_out, or_6_out, or_7_out, sevensegdecoder_1_1_a,
       sevensegdecoder_1_1_b, sevensegdecoder_1_1_c, sevensegdecoder_1_1_d, sevensegdecoder_1_1_e,
       sevensegdecoder_1_1_f, sevensegdecoder_1_1_g, sevensegdecoder_1_1_point, sevensegdecoder_1_2_a,
       sevensegdecoder_1_2_b, sevensegdecoder_1_2_c, sevensegdecoder_1_2_d, sevensegdecoder_1_2_e,
       sevensegdecoder_1_2_f, sevensegdecoder_1_2_g, sevensegdecoder_1_2_point, sevensegdecoder_1_3_a,
       sevensegdecoder_1_3_b, sevensegdecoder_1_3_c, sevensegdecoder_1_3_d, sevensegdecoder_1_3_e,
       sevensegdecoder_1_3_f, sevensegdecoder_1_3_g, sevensegdecoder_1_3_point, sevensegdecoder_1_4_a,
       sevensegdecoder_1_4_b, sevensegdecoder_1_4_c, sevensegdecoder_1_4_d, sevensegdecoder_1_4_e,
       sevensegdecoder_1_4_f, sevensegdecoder_1_4_g, sevensegdecoder_1_4_point, sevensegdecoder_1_5_a,
       sevensegdecoder_1_5_b, sevensegdecoder_1_5_c, sevensegdecoder_1_5_d, sevensegdecoder_1_5_e,
       sevensegdecoder_1_5_f, sevensegdecoder_1_5_g, sevensegdecoder_1_5_point, sevensegdecoder_1_6_a,
       sevensegdecoder_1_6_b, sevensegdecoder_1_6_c, sevensegdecoder_1_6_d, sevensegdecoder_1_6_e,
       sevensegdecoder_1_6_f, sevensegdecoder_1_6_g, sevensegdecoder_1_6_point;
  wire [3:0] register4bit_1_q0, register4bit_2_q0, register4bit_3_q0, register4bit_4_q0, register4bit_5_q0,
       register4bit_6_q0;

  and and_1 (and_1_out, and_5_out, or_2_out);
  or or_1 (or_1_out, and_1_out, R);
  register4bit register4bit_1 (
    .D0(adder4bit_1_y0), .D1(adder4bit_1_y1), .D2(adder4bit_1_y2), .D3(adder4bit_1_y3), .EN(and_5_out),
    .CLK(CLK_out), .R(or_1_out), .Q0(register4bit_1_q0[0]), .Q1(register4bit_1_q0[1]),
    .Q2(register4bit_1_q0[2]), .Q3(register4bit_1_q0[3]));
  Adder4bit adder4bit_1 (
    .Cin(1'b0), .A0(register4bit_1_q0[0]), .A1(register4bit_1_q0[1]), .A2(register4bit_1_q0[2]),
    .A3(register4bit_1_q0[3]), .B0(1'b1), .B1(1'b0), .B2(1'b0), .B3(1'b0), .Y0(adder4bit_1_y0),
    .Y1(adder4bit_1_y1), .Y2(adder4bit_1_y2), .Y3(adder4bit_1_y3));  // open: Cout
  Comparator #(.mode("unsigned"), .width(4)) comparator_1 (
    .a(register4bit_1_q0), .b(4'b1001), .eq(comparator_1_eq));  // open: gt, lt
  Comparator #(.mode("unsigned"), .width(4)) comparator_2 (
    .a(register4bit_1_q0), .b(4'b0011), .eq(comparator_2_eq));  // open: gt, lt
  and and_2 (and_2_out, comparator_2_eq, comparator_3_eq);
  or or_2 (or_2_out, comparator_1_eq, and_2_out);
  SevenSegDecoder_1 sevensegdecoder_1_1 (
    .A0(register4bit_1_q0[0]), .A1(register4bit_1_q0[1]), .A2(register4bit_1_q0[2]),
    .A3(register4bit_1_q0[3]), .EN(1'b1), .A(sevensegdecoder_1_1_a), .B(sevensegdecoder_1_1_b),
    .C(sevensegdecoder_1_1_c), .D(sevensegdecoder_1_1_d), .E(sevensegdecoder_1_1_e),
    .F(sevensegdecoder_1_1_f), .G(sevensegdecoder_1_1_g), .point(sevensegdecoder_1_1_point));
  and and_3 (and_3_out, and_1_out, and_2_out);
  or or_3 (or_3_out, and_3_out, R);
  register4bit register4bit_2 (
    .D0(adder4bit_2_y0), .D1(adder4bit_2_y1), .D2(adder4bit_2_y2), .D3(adder4bit_2_y3), .EN(and_1_out),
    .CLK(CLK_out), .R(or_3_out), .Q0(register4bit_2_q0[0]), .Q1(register4bit_2_q0[1]),
    .Q2(register4bit_2_q0[2]), .Q3(register4bit_2_q0[3]));
  Adder4bit adder4bit_2 (
    .Cin(1'b0), .A0(register4bit_2_q0[0]), .A1(register4bit_2_q0[1]), .A2(register4bit_2_q0[2]),
    .A3(register4bit_2_q0[3]), .B0(1'b1), .B1(1'b0), .B2(1'b0), .B3(1'b0), .Y0(adder4bit_2_y0),
    .Y1(adder4bit_2_y1), .Y2(adder4bit_2_y2), .Y3(adder4bit_2_y3));  // open: Cout
  Comparator #(.mode("unsigned"), .width(4)) comparator_3 (
    .a(register4bit_2_q0), .b(4'b0010), .eq(comparator_3_eq));  // open: gt, lt
  SevenSegDecoder_1 sevensegdecoder_1_2 (
    .A0(register4bit_2_q0[0]), .A1(register4bit_2_q0[1]), .A2(register4bit_2_q0[2]),
    .A3(register4bit_2_q0[3]), .EN(1'b1), .A(sevensegdecoder_1_2_a), .B(sevensegdecoder_1_2_b),
    .C(sevensegdecoder_1_2_c), .D(sevensegdecoder_1_2_d), .E(sevensegdecoder_1_2_e),
    .F(sevensegdecoder_1_2_f), .G(sevensegdecoder_1_2_g), .point(sevensegdecoder_1_2_point));
  Clock CLK (.out(CLK_out));
  _7_Segment_Display u_7_segment_display_1 (
    .g(sevensegdecoder_1_2_g), .f(sevensegdecoder_1_2_f), .a(sevensegdecoder_1_2_a),
    .b(sevensegdecoder_1_2_b), .e(sevensegdecoder_1_2_e), .d(sevensegdecoder_1_2_d),
    .c(sevensegdecoder_1_2_c), .dp(sevensegdecoder_1_2_point));
  _7_Segment_Display u_7_segment_display_2 (
    .g(sevensegdecoder_1_1_g), .f(sevensegdecoder_1_1_f), .a(sevensegdecoder_1_1_a),
    .b(sevensegdecoder_1_1_b), .e(sevensegdecoder_1_1_e), .d(sevensegdecoder_1_1_d),
    .c(sevensegdecoder_1_1_c), .dp(sevensegdecoder_1_1_point));
  and and_4 (and_4_out, and_6_out, comparator_4_eq);
  or or_4 (or_4_out, and_4_out, R);
  or or_5 (or_5_out, comparator_5_eq, R);
  register4bit register4bit_3 (
    .D0(adder4bit_3_y0), .D1(adder4bit_3_y1), .D2(adder4bit_3_y2), .D3(adder4bit_3_y3), .EN(and_6_out),
    .CLK(CLK_out), .R(or_4_out), .Q0(register4bit_3_q0[0]), .Q1(register4bit_3_q0[1]),
    .Q2(register4bit_3_q0[2]), .Q3(register4bit_3_q0[3]));
  Adder4bit adder4bit_3 (
    .Cin(1'b0), .A0(register4bit_3_q0[0]), .A1(register4bit_3_q0[1]), .A2(register4bit_3_q0[2]),
    .A3(register4bit_3_q0[3]), .B0(1'b1), .B1(1'b0), .B2(1'b0), .B3(1'b0), .Y0(adder4bit_3_y0),
    .Y1(adder4bit_3_y1), .Y2(adder4bit_3_y2), .Y3(adder4bit_3_y3));  // open: Cout
  _7_Segment_Display u_7_segment_display_3 (
    .g(sevensegdecoder_1_5_g), .f(sevensegdecoder_1_5_f), .a(sevensegdecoder_1_5_a),
    .b(sevensegdecoder_1_5_b), .e(sevensegdecoder_1_5_e), .d(sevensegdecoder_1_5_d),
    .c(sevensegdecoder_1_5_c), .dp(sevensegdecoder_1_5_point));
  register4bit register4bit_4 (
    .D0(adder4bit_4_y0), .D1(adder4bit_4_y1), .D2(adder4bit_4_y2), .D3(adder4bit_4_y3), .EN(1'b1),
    .CLK(CLK_out), .R(or_5_out), .Q0(register4bit_4_q0[0]), .Q1(register4bit_4_q0[1]),
    .Q2(register4bit_4_q0[2]), .Q3(register4bit_4_q0[3]));
  Adder4bit adder4bit_4 (
    .Cin(1'b0), .A0(register4bit_4_q0[0]), .A1(register4bit_4_q0[1]), .A2(register4bit_4_q0[2]),
    .A3(register4bit_4_q0[3]), .B0(1'b1), .B1(1'b0), .B2(1'b0), .B3(1'b0), .Y0(adder4bit_4_y0),
    .Y1(adder4bit_4_y1), .Y2(adder4bit_4_y2), .Y3(adder4bit_4_y3));  // open: Cout
  _7_Segment_Display u_7_segment_display_4 (
    .g(sevensegdecoder_1_3_g), .f(sevensegdecoder_1_3_f), .a(sevensegdecoder_1_3_a),
    .b(sevensegdecoder_1_3_b), .e(sevensegdecoder_1_3_e), .d(sevensegdecoder_1_3_d),
    .c(sevensegdecoder_1_3_c), .dp(sevensegdecoder_1_3_point));
  Comparator #(.mode("unsigned"), .width(4)) comparator_4 (
    .a(register4bit_3_q0), .b(4'b1001), .eq(comparator_4_eq));  // open: gt, lt
  Comparator #(.mode("unsigned"), .width(4)) comparator_5 (
    .a(register4bit_4_q0), .b(4'b1001), .eq(comparator_5_eq));  // open: gt, lt
  SevenSegDecoder_1 sevensegdecoder_1_3 (
    .A0(register4bit_3_q0[0]), .A1(register4bit_3_q0[1]), .A2(register4bit_3_q0[2]),
    .A3(register4bit_3_q0[3]), .EN(1'b1), .A(sevensegdecoder_1_3_a), .B(sevensegdecoder_1_3_b),
    .C(sevensegdecoder_1_3_c), .D(sevensegdecoder_1_3_d), .E(sevensegdecoder_1_3_e),
    .F(sevensegdecoder_1_3_f), .G(sevensegdecoder_1_3_g), .point(sevensegdecoder_1_3_point));
  _7_Segment_Display u_7_segment_display_5 (
    .g(sevensegdecoder_1_6_g), .f(sevensegdecoder_1_6_f), .a(sevensegdecoder_1_6_a),
    .b(sevensegdecoder_1_6_b), .e(sevensegdecoder_1_6_e), .d(sevensegdecoder_1_6_d),
    .c(sevensegdecoder_1_6_c), .dp(sevensegdecoder_1_6_point));
  SevenSegDecoder_1 sevensegdecoder_1_4 (
    .A0(register4bit_4_q0[0]), .A1(register4bit_4_q0[1]), .A2(register4bit_4_q0[2]),
    .A3(register4bit_4_q0[3]), .EN(1'b1), .A(sevensegdecoder_1_4_a), .B(sevensegdecoder_1_4_b),
    .C(sevensegdecoder_1_4_c), .D(sevensegdecoder_1_4_d), .E(sevensegdecoder_1_4_e),
    .F(sevensegdecoder_1_4_f), .G(sevensegdecoder_1_4_g), .point(sevensegdecoder_1_4_point));
  _7_Segment_Display u_7_segment_display_6 (
    .g(sevensegdecoder_1_4_g), .f(sevensegdecoder_1_4_f), .a(sevensegdecoder_1_4_a),
    .b(sevensegdecoder_1_4_b), .e(sevensegdecoder_1_4_e), .d(sevensegdecoder_1_4_d),
    .c(sevensegdecoder_1_4_c), .dp(sevensegdecoder_1_4_point));
  and and_5 (and_5_out, and_4_out, comparator_6_eq);
  and and_6 (and_6_out, comparator_5_eq, comparator_7_eq);
  or or_6 (or_6_out, and_5_out, R);
  or or_7 (or_7_out, and_6_out, R);
  register4bit register4bit_5 (
    .D0(adder4bit_5_y0), .D1(adder4bit_5_y1), .D2(adder4bit_5_y2), .D3(adder4bit_5_y3), .EN(and_4_out),
    .CLK(CLK_out), .R(or_6_out), .Q0(register4bit_5_q0[0]), .Q1(register4bit_5_q0[1]),
    .Q2(register4bit_5_q0[2]), .Q3(register4bit_5_q0[3]));
  Adder4bit adder4bit_5 (
    .Cin(1'b0), .A0(register4bit_5_q0[0]), .A1(register4bit_5_q0[1]), .A2(register4bit_5_q0[2]),
    .A3(register4bit_5_q0[3]), .B0(1'b1), .B1(1'b0), .B2(1'b0), .B3(1'b0), .Y0(adder4bit_5_y0),
    .Y1(adder4bit_5_y1), .Y2(adder4bit_5_y2), .Y3(adder4bit_5_y3));  // open: Cout
  register4bit register4bit_6 (
    .D0(adder4bit_6_y0), .D1(adder4bit_6_y1), .D2(adder4bit_6_y2), .D3(adder4bit_6_y3), .EN(comparator_5_eq),
    .CLK(CLK_out), .R(or_7_out), .Q0(register4bit_6_q0[0]), .Q1(register4bit_6_q0[1]),
    .Q2(register4bit_6_q0[2]), .Q3(register4bit_6_q0[3]));
  Adder4bit adder4bit_6 (
    .Cin(1'b0), .A0(register4bit_6_q0[0]), .A1(register4bit_6_q0[1]), .A2(register4bit_6_q0[2]),
    .A3(register4bit_6_q0[3]), .B0(1'b1), .B1(1'b0), .B2(1'b0), .B3(1'b0), .Y0(adder4bit_6_y0),
    .Y1(adder4bit_6_y1), .Y2(adder4bit_6_y2), .Y3(adder4bit_6_y3));  // open: Cout
  Comparator #(.mode("unsigned"), .width(4)) comparator_6 (
    .a(register4bit_5_q0), .b(4'b0101), .eq(comparator_6_eq));  // open: gt, lt
  Comparator #(.mode("unsigned"), .width(4)) comparator_7 (
    .a(register4bit_6_q0), .b(4'b0101), .eq(comparator_7_eq));  // open: gt, lt
  SevenSegDecoder_1 sevensegdecoder_1_5 (
    .A0(register4bit_5_q0[0]), .A1(register4bit_5_q0[1]), .A2(register4bit_5_q0[2]),
    .A3(register4bit_5_q0[3]), .EN(1'b1), .A(sevensegdecoder_1_5_a), .B(sevensegdecoder_1_5_b),
    .C(sevensegdecoder_1_5_c), .D(sevensegdecoder_1_5_d), .E(sevensegdecoder_1_5_e),
    .F(sevensegdecoder_1_5_f), .G(sevensegdecoder_1_5_g), .point(sevensegdecoder_1_5_point));
  SevenSegDecoder_1 sevensegdecoder_1_6 (
    .A0(register4bit_6_q0[0]), .A1(register4bit_6_q0[1]), .A2(register4bit_6_q0[2]),
    .A3(register4bit_6_q0[3]), .EN(1'b1), .A(sevensegdecoder_1_6_a), .B(sevensegdecoder_1_6_b),
    .C(sevensegdecoder_1_6_c), .D(sevensegdecoder_1_6_d), .E(sevensegdecoder_1_6_e),
    .F(sevensegdecoder_1_6_f), .G(sevensegdecoder_1_6_g), .point(sevensegdecoder_1_6_point));
endmodule

module sCPU_1 (
  input  R,
  output [7:0] r0,
  output [7:0] r1,
  output [7:0] r2,
  output [7:0] out_5,
  output [7:0] r3
);

  wire and_1_out, CLK_out, comparator_1_eq, decoder2to4_1_q0, decoder2to4_1_q2, decoder2to4_1_q3, not_1_out,
       or_1_out, register8bit_1_q3, register8bit_1_q4, register8bit_1_q5, register8bit_1_q6,
       register8bit_1_q7;
  wire [2:0] register8bit_1_q0;
  wire [7:0] adder8bit_1_q0, adder_1_out, multiplexer_1_out, multiplexer_3_out, ram4x8_1_readdata1,
       ram4x8_1_readdata2;

  Clock CLK (.out(CLK_out));
  Multiplexer #(.width(8)) multiplexer_1 (
    .in0(adder8bit_1_q0), .in1({4'b0000, out_5[5:2]}), .out(multiplexer_1_out), .sel(and_1_out));
  register8bit register8bit_1 (
    .D0(multiplexer_1_out[0]), .D1(multiplexer_1_out[1]), .D2(multiplexer_1_out[2]),
    .D3(multiplexer_1_out[3]), .D4(multiplexer_1_out[4]), .D5(multiplexer_1_out[5]),
    .D6(multiplexer_1_out[6]), .D7(multiplexer_1_out[7]), .EN(1'b1), .CLK(CLK_out), .R(R),
    .Q0(register8bit_1_q0[0]), .Q1(register8bit_1_q0[1]), .Q2(register8bit_1_q0[2]), .Q3(register8bit_1_q3),
    .Q4(register8bit_1_q4), .Q5(register8bit_1_q5), .Q6(register8bit_1_q6), .Q7(register8bit_1_q7));
  Adder8bit adder8bit_1 (
    .Cin(1'b0), .A0(register8bit_1_q0[0]), .A1(register8bit_1_q0[1]), .A2(register8bit_1_q0[2]),
    .A3(register8bit_1_q3), .A4(register8bit_1_q4), .A5(register8bit_1_q5), .A6(register8bit_1_q6),
    .A7(register8bit_1_q7), .B0(1'b1), .B1(1'b0), .B2(1'b0), .B3(1'b0), .B4(1'b0), .B5(1'b0), .B6(1'b0),
    .B7(1'b0), .Q0(adder8bit_1_q0[0]), .Q1(adder8bit_1_q0[1]), .Q2(adder8bit_1_q0[2]),
    .Q3(adder8bit_1_q0[3]), .Q4(adder8bit_1_q0[4]), .Q5(adder8bit_1_q0[5]), .Q6(adder8bit_1_q0[6]),
    .Q7(adder8bit_1_q0[7]));  // open: Cout
  Multiplexer #(.select(3), .width(8)) multiplexer_2 (
    .in0(8'h8a), .in1(8'h90), .in2(8'ha0), .in3(8'hb1), .in4(8'h17), .in5(8'h29), .in6(8'hd1), .in7(8'hdf),
    .out(out_5), .sel(register8bit_1_q0));
  Decoder2to4 decoder2to4_1 (
    .A0(out_5[6]), .A1(out_5[7]), .EN(1'b1), .Q0(decoder2to4_1_q0), .Q2(decoder2to4_1_q2),
    .Q3(decoder2to4_1_q3));  // open: Q1
  Multiplexer #(.width(8)) multiplexer_3 (
    .in0(adder_1_out), .in1({4'b0000, out_5[3:0]}), .out(multiplexer_3_out), .sel(decoder2to4_1_q2));
  or or_1 (or_1_out, decoder2to4_1_q0, decoder2to4_1_q2);
  RAM4x8 ram4x8_1 (
    .Writedata(multiplexer_3_out), .rd(out_5[5:4]), .rs1(out_5[3:2]), .rs2(out_5[1:0]), .WE(or_1_out),
    .CLK(CLK_out), .R(R), .Readdata1(ram4x8_1_readdata1), .Readdata2(ram4x8_1_readdata2), .r0(r0), .r1(r1),
    .r2(r2), .r3(r3));
  Adder adder_1 (.a(ram4x8_1_readdata1), .b(ram4x8_1_readdata2), .out(adder_1_out), .cin(1'b0));  // open: cout
  Comparator #(.mode("unsigned")) comparator_1 (.a(ram4x8_1_readdata2), .b(r0), .eq(comparator_1_eq));  // open: gt, lt
  not not_1 (not_1_out, comparator_1_eq);
  and and_1 (and_1_out, not_1_out, decoder2to4_1_q3);
endmodule

module RAM4x8 (
  input  [7:0] Writedata,
  input  [1:0] rd,
  input  [1:0] rs1,
  input  [1:0] rs2,
  input  WE,
  input  CLK,
  input  R,
  output [7:0] Readdata1,
  output [7:0] Readdata2,
  output [7:0] r0,
  output [7:0] r1,
  output [7:0] r2,
  output [7:0] r3
);

  wire decoder2to4_1_q0, decoder2to4_1_q1, decoder2to4_1_q2, decoder2to4_1_q3;

  Decoder2to4 decoder2to4_1 (
    .A0(rd[0]), .A1(rd[1]), .EN(WE), .Q0(decoder2to4_1_q0), .Q1(decoder2to4_1_q1), .Q2(decoder2to4_1_q2),
    .Q3(decoder2to4_1_q3));
  register8bit register8bit_1 (
    .D0(Writedata[0]), .D1(Writedata[1]), .D2(Writedata[2]), .D3(Writedata[3]), .D4(Writedata[4]),
    .D5(Writedata[5]), .D6(Writedata[6]), .D7(Writedata[7]), .EN(decoder2to4_1_q0), .CLK(CLK), .R(R),
    .Q0(r0[0]), .Q1(r0[1]), .Q2(r0[2]), .Q3(r0[3]), .Q4(r0[4]), .Q5(r0[5]), .Q6(r0[6]), .Q7(r0[7]));
  register8bit register8bit_2 (
    .D0(Writedata[0]), .D1(Writedata[1]), .D2(Writedata[2]), .D3(Writedata[3]), .D4(Writedata[4]),
    .D5(Writedata[5]), .D6(Writedata[6]), .D7(Writedata[7]), .EN(decoder2to4_1_q1), .CLK(CLK), .R(R),
    .Q0(r1[0]), .Q1(r1[1]), .Q2(r1[2]), .Q3(r1[3]), .Q4(r1[4]), .Q5(r1[5]), .Q6(r1[6]), .Q7(r1[7]));
  register8bit register8bit_3 (
    .D0(Writedata[0]), .D1(Writedata[1]), .D2(Writedata[2]), .D3(Writedata[3]), .D4(Writedata[4]),
    .D5(Writedata[5]), .D6(Writedata[6]), .D7(Writedata[7]), .EN(decoder2to4_1_q2), .CLK(CLK), .R(R),
    .Q0(r2[0]), .Q1(r2[1]), .Q2(r2[2]), .Q3(r2[3]), .Q4(r2[4]), .Q5(r2[5]), .Q6(r2[6]), .Q7(r2[7]));
  register8bit register8bit_4 (
    .D0(Writedata[0]), .D1(Writedata[1]), .D2(Writedata[2]), .D3(Writedata[3]), .D4(Writedata[4]),
    .D5(Writedata[5]), .D6(Writedata[6]), .D7(Writedata[7]), .EN(decoder2to4_1_q3), .CLK(CLK), .R(R),
    .Q0(r3[0]), .Q1(r3[1]), .Q2(r3[2]), .Q3(r3[3]), .Q4(r3[4]), .Q5(r3[5]), .Q6(r3[6]), .Q7(r3[7]));
  Multiplexer #(.select(2), .width(8)) multiplexer_1 (
    .in0(r0), .in1(r1), .in2(r2), .in3(r3), .out(Readdata1), .sel(rs1));
  Multiplexer #(.select(2), .width(8)) multiplexer_2 (
    .in0(r0), .in1(r1), .in2(r2), .in3(r3), .out(Readdata2), .sel(rs2));
endmodule

module ROM8x8 (
  input  R,
  output [7:0] out_2
);

  wire adder8bit_1_q0, adder8bit_1_q1, adder8bit_1_q2, adder8bit_1_q3, adder8bit_1_q4, adder8bit_1_q5,
       adder8bit_1_q6, adder8bit_1_q7, CLK_out, comparator_1_lt, register8bit_1_q3, register8bit_1_q4,
       register8bit_1_q5, register8bit_1_q6, register8bit_1_q7;
  wire [2:0] register8bit_1_q0;

  Clock CLK (.out(CLK_out));
  register8bit register8bit_1 (
    .D0(adder8bit_1_q0), .D1(adder8bit_1_q1), .D2(adder8bit_1_q2), .D3(adder8bit_1_q3), .D4(adder8bit_1_q4),
    .D5(adder8bit_1_q5), .D6(adder8bit_1_q6), .D7(adder8bit_1_q7), .EN(comparator_1_lt), .CLK(CLK_out),
    .R(R), .Q0(register8bit_1_q0[0]), .Q1(register8bit_1_q0[1]), .Q2(register8bit_1_q0[2]),
    .Q3(register8bit_1_q3), .Q4(register8bit_1_q4), .Q5(register8bit_1_q5), .Q6(register8bit_1_q6),
    .Q7(register8bit_1_q7));
  Adder8bit adder8bit_1 (
    .Cin(1'b0), .A0(register8bit_1_q0[0]), .A1(register8bit_1_q0[1]), .A2(register8bit_1_q0[2]),
    .A3(register8bit_1_q3), .A4(register8bit_1_q4), .A5(register8bit_1_q5), .A6(register8bit_1_q6),
    .A7(register8bit_1_q7), .B0(1'b1), .B1(1'b0), .B2(1'b0), .B3(1'b0), .B4(1'b0), .B5(1'b0), .B6(1'b0),
    .B7(1'b0), .Q0(adder8bit_1_q0), .Q1(adder8bit_1_q1), .Q2(adder8bit_1_q2), .Q3(adder8bit_1_q3),
    .Q4(adder8bit_1_q4), .Q5(adder8bit_1_q5), .Q6(adder8bit_1_q6), .Q7(adder8bit_1_q7));  // open: Cout
  Comparator #(.mode("unsigned"), .width(3)) comparator_1 (
    .a(register8bit_1_q0), .b(3'b111), .lt(comparator_1_lt));  // open: gt, eq
  Multiplexer #(.select(3), .width(8)) multiplexer_1 (
    .in0(8'h8a), .in1(8'h90), .in2(8'ha0), .in3(8'hb1), .in4(8'h17), .in5(8'h29), .in6(8'hd1), .in7(8'hdf),
    .out(out_2), .sel(register8bit_1_q0));
endmodule

module sCPU_2 (
  input  R,
  output [7:0] r0,
  output [7:0] r1,
  output [7:0] r2,
  output [7:0] r3,
  output [7:0] out_6
);

  wire adder8bit_1_q0, adder8bit_1_q1, adder8bit_1_q2, adder8bit_1_q3, adder8bit_1_q4, adder8bit_1_q5,
       adder8bit_1_q6, adder8bit_1_q7, and_1_out, and_2_out, and_3_out, and_4_out, and_5_out, CLK_out,
       comparator_1_eq, decoder2to4_1_q0, decoder2to4_1_q1, decoder2to4_1_q2, decoder2to4_1_q3, not_1_out,
       not_2_out, not_3_out, not_4_out, not_5_out, or_1_out, register8bit_1_q4, register8bit_1_q5,
       register8bit_1_q6, register8bit_1_q7, register8bit_2_q0, register8bit_2_q1, register8bit_2_q2,
       register8bit_2_q3, register8bit_2_q4, register8bit_2_q5, register8bit_2_q6, register8bit_2_q7;
  wire [1:0] multiplexer_3_out;
  wire [3:0] register8bit_1_q0, register8bit_3_q0, register8bit_3_q4;
  wire [7:0] adder_1_out, B0_out, dipswitch_1_p1, multiplexer_1_out, multiplexer_4_out, multiplexer_5_out,
       multiplexer_6_out, multiplexer_7_out, ram4x8_1_readdata1, ram4x8_1_readdata2;

  Clock CLK (.out(CLK_out));
  Multiplexer #(.width(8)) multiplexer_1 (
    .in0(8'h1), .in1({{5{out_6[5]}}, out_6[4:2]}), .out(multiplexer_1_out), .sel(and_5_out));
  register8bit register8bit_1 (
    .D0(adder8bit_1_q0), .D1(adder8bit_1_q1), .D2(adder8bit_1_q2), .D3(adder8bit_1_q3), .D4(adder8bit_1_q4),
    .D5(adder8bit_1_q5), .D6(adder8bit_1_q6), .D7(adder8bit_1_q7), .EN(1'b1), .CLK(CLK_out), .R(R),
    .Q0(register8bit_1_q0[0]), .Q1(register8bit_1_q0[1]), .Q2(register8bit_1_q0[2]),
    .Q3(register8bit_1_q0[3]), .Q4(register8bit_1_q4), .Q5(register8bit_1_q5), .Q6(register8bit_1_q6),
    .Q7(register8bit_1_q7));
  Adder8bit adder8bit_1 (
    .Cin(1'b0), .A0(register8bit_1_q0[0]), .A1(register8bit_1_q0[1]), .A2(register8bit_1_q0[2]),
    .A3(register8bit_1_q0[3]), .A4(register8bit_1_q4), .A5(register8bit_1_q5), .A6(register8bit_1_q6),
    .A7(register8bit_1_q7), .B0(multiplexer_1_out[0]), .B1(multiplexer_1_out[1]), .B2(multiplexer_1_out[2]),
    .B3(multiplexer_1_out[3]), .B4(multiplexer_1_out[4]), .B5(multiplexer_1_out[5]),
    .B6(multiplexer_1_out[6]), .B7(multiplexer_1_out[7]), .Q0(adder8bit_1_q0), .Q1(adder8bit_1_q1),
    .Q2(adder8bit_1_q2), .Q3(adder8bit_1_q3), .Q4(adder8bit_1_q4), .Q5(adder8bit_1_q5), .Q6(adder8bit_1_q6),
    .Q7(adder8bit_1_q7));  // open: Cout
  Multiplexer #(.select(4), .width(8)) multiplexer_2 (
    .in0(8'h81), .in1(8'h91), .in2(8'ha0), .in3(8'h29), .in4(8'h58), .in5(8'h69), .in6(8'h14), .in7(8'h71),
    .in8({8{1'b1}}), .in9(8'h71), .in10(8'he7), .in11(8'hf9), .out(out_6), .sel(register8bit_1_q0));  // open: in12, in13, in14, in15
  Multiplexer #(.width(2)) multiplexer_3 (.in0(out_6[3:2]), .in1(out_6[5:4]), .out(multiplexer_3_out), .sel(and_2_out));
  Multiplexer #(.select(2), .width(8)) multiplexer_4 (
    .in0({{6{1'b0}}, out_6[1:0]}), .in1({4'b0000, out_6[1:0], 2'b00}), .in2({2'b00, out_6[1:0], 4'b0000}),
    .in3({out_6[1:0], {6{1'b0}}}), .out(multiplexer_4_out), .sel(out_6[3:2]));
  Decoder2to4 decoder2to4_1 (
    .A0(out_6[6]), .A1(out_6[7]), .EN(1'b1), .Q0(decoder2to4_1_q0), .Q1(decoder2to4_1_q1),
    .Q2(decoder2to4_1_q2), .Q3(decoder2to4_1_q3));
  not not_1 (not_1_out, out_6[3]);
  Multiplexer #(.width(8)) multiplexer_5 (
    .in0(adder_1_out), .in1(multiplexer_4_out), .out(multiplexer_5_out), .sel(decoder2to4_1_q2));
  Multiplexer #(.width(8)) multiplexer_6 (
    .in0(multiplexer_5_out), .in1(multiplexer_7_out), .out(multiplexer_6_out), .sel(and_1_out));
  or or_1 (or_1_out, decoder2to4_1_q0, and_1_out, decoder2to4_1_q2);
  and and_1 (and_1_out, decoder2to4_1_q1, not_1_out);
  and and_2 (and_2_out, decoder2to4_1_q1, out_6[3]);
  not not_2 (not_2_out, out_6[2]);
  not not_3 (not_3_out, out_6[1]);
  not not_4 (not_4_out, out_6[0]);
  and and_3 (and_3_out, and_2_out, not_2_out, not_3_out, not_4_out);
  and and_4 (and_4_out, and_2_out, not_2_out, out_6[0]);
  Multiplexer #(.select(3), .width(8)) multiplexer_7 (
    .in0(dipswitch_1_p1), .in1(B0_out), .out(multiplexer_7_out), .sel(out_6[2:0]));  // open: in2, in3, in4, in5, in6, in7
  RAM4x8 ram4x8_1 (
    .Writedata(multiplexer_6_out), .rd(out_6[5:4]), .rs1(multiplexer_3_out), .rs2(out_6[1:0]), .WE(or_1_out),
    .CLK(CLK_out), .R(R), .Readdata1(ram4x8_1_readdata1), .Readdata2(ram4x8_1_readdata2), .r0(r0), .r1(r1),
    .r2(r2), .r3(r3));
  Adder adder_1 (.a(ram4x8_1_readdata1), .b(ram4x8_1_readdata2), .out(adder_1_out), .cin(1'b0));  // open: cout
  // DipSwitch dipswitch_1: pin names not known; wires that end beside it: dipswitch_1_p1[0], dipswitch_1_p1[1], dipswitch_1_p1[2], dipswitch_1_p1[3], dipswitch_1_p1[4], dipswitch_1_p1[5], dipswitch_1_p1[6], dipswitch_1_p1[7]
  Button B0 (.out(B0_out[0]));
  Button B1 (.out(B0_out[1]));
  Button B2 (.out(B0_out[2]));
  Button B3 (.out(B0_out[3]));
  Button B4 (.out(B0_out[4]));
  Button B5 (.out(B0_out[5]));
  Button B6 (.out(B0_out[6]));
  Button B7 (.out(B0_out[7]));
  Comparator #(.mode("unsigned")) comparator_1 (.a(ram4x8_1_readdata2), .b(r0), .eq(comparator_1_eq));  // open: gt, lt
  not not_5 (not_5_out, comparator_1_eq);
  and and_5 (and_5_out, not_5_out, decoder2to4_1_q3);
  register8bit register8bit_2 (
    .D0(ram4x8_1_readdata1[0]), .D1(ram4x8_1_readdata1[1]), .D2(ram4x8_1_readdata1[2]),
    .D3(ram4x8_1_readdata1[3]), .D4(ram4x8_1_readdata1[4]), .D5(ram4x8_1_readdata1[5]),
    .D6(ram4x8_1_readdata1[6]), .D7(ram4x8_1_readdata1[7]), .EN(and_3_out), .CLK(CLK_out), .R(R),
    .Q0(register8bit_2_q0), .Q1(register8bit_2_q1), .Q2(register8bit_2_q2), .Q3(register8bit_2_q3),
    .Q4(register8bit_2_q4), .Q5(register8bit_2_q5), .Q6(register8bit_2_q6), .Q7(register8bit_2_q7));
  LedBar ledbar_1 (
    .led0(register8bit_2_q7), .led1(register8bit_2_q6), .led2(register8bit_2_q5), .led3(register8bit_2_q4),
    .led4(register8bit_2_q3), .led5(register8bit_2_q2), .led6(register8bit_2_q1), .led7(register8bit_2_q0));
  register8bit register8bit_3 (
    .D0(ram4x8_1_readdata1[0]), .D1(ram4x8_1_readdata1[1]), .D2(ram4x8_1_readdata1[2]),
    .D3(ram4x8_1_readdata1[3]), .D4(ram4x8_1_readdata1[4]), .D5(ram4x8_1_readdata1[5]),
    .D6(ram4x8_1_readdata1[6]), .D7(ram4x8_1_readdata1[7]), .EN(and_4_out), .CLK(CLK_out), .R(R),
    .Q0(register8bit_3_q0[0]), .Q1(register8bit_3_q0[1]), .Q2(register8bit_3_q0[2]),
    .Q3(register8bit_3_q0[3]), .Q4(register8bit_3_q4[0]), .Q5(register8bit_3_q4[1]),
    .Q6(register8bit_3_q4[2]), .Q7(register8bit_3_q4[3]));
  Hex_Digit_Display #(.decimalPoint("false")) hex_digit_display_1 (.value(register8bit_3_q4));
  Hex_Digit_Display #(.decimalPoint("false")) hex_digit_display_2 (.value(register8bit_3_q0));
endmodule
